# Fritzing sketch Circuit Diagram (saved by Fritzing 0.9.3b)

parts:
  Red_Button = Round Pushbutton
  Raspberry_Pi1 = Raspberry Pi 2
  Red_LED = smd LED [color="Red (633nm)" package="0805 [SMD]"]
  Green_LED = smd LED [color="Green (570nm)" package="0805 [SMD]"]
  Green_Button = Round Pushbutton

nets:
  N1: Red_Button.leg0, Raspberry_Pi1.GND, Red_LED.cathode, Green_LED.cathode, Green_Button.leg0
  N2: Red_Button.leg1, Raspberry_Pi1.GPIO17
  N3: Raspberry_Pi1.GPIO27, Green_Button.leg1
  N4: Raspberry_Pi1.GPIO23, Green_LED.anode
  N5: Raspberry_Pi1.GPIO18, Red_LED.anode
