# Fritzing sketch Circuit Diagram (saved by Fritzing 0.9.3b)
breadboards: 1

parts:
  Raspberry_Pi1 = Raspberry Pi B+
  S1 = Momentary Switch [package=tactile-pth]  # not connected
  S2 = Round Pushbutton

nets:
  N1: Raspberry_Pi1.GPIO5, S2.leg1
  N2: Raspberry_Pi1.5V, S2.leg0
